// Logisim project new.circ as structural Verilog: 2 circuits, main circuit main
// *-BIT_SUBTRACTOR
module _8_bit_subtractor (
  input  [7:0] Y,
  input  [7:0] X,
  output [7:0] out_3,
  output out_4
);

  wire adder_1_cout;
  wire [7:0] adder_1_out, not_1_out;

  assign not_1_out = ~Y;  // NOT_Gate not_1, 8 bits wide
  Adder adder_1 (.a(8'h1), .b(not_1_out), .out(adder_1_out), .cin(1'b0), .cout(adder_1_cout));
  Adder adder_2 (.a(adder_1_out), .b(X), .out(out_3), .cin(adder_1_cout), .cout(out_4));
endmodule

module main (
  input  [2:0] OpCode,
  input  [7:0] Y,
  input  [7:0] X,
  output out_4,
  output [7:0] out_5,
  output out_6,
  output EQ,
  output SF,
  output CF,
  output ZF,
  output OF,
  output SF_2,
  output ZF_2,
  output CF_2,
  output OF_2,
  output EQ_2
);

  wire and_1_out, and_2_out, and_3_out, and_4_out, and_5_out, and_6_out, and_7_out, and_8_out, and_9_out,
       and_10_out, and_12_out, and_13_out, and_14_out, and_15_out, comparator_2_eq, nor_1_out, not_1_out,
       not_2_out, not_4_out, not_5_out, not_6_out, not_7_out, not_8_out, or_2_out, or_3_out;
  wire [7:0] adder_1_out, adder_2_out, AND_11_out, bit_extender_1_out, not_3_out, OR_out, shifter_1_out,
       shifter_2_out, shifter_3_out;

  not not_1 (not_1_out, Y[7]);
  and and_1 (and_1_out, Y[7], X[7]);
  and and_2 (and_2_out, Y[7], not_2_out);
  not not_2 (not_2_out, X[7]);
  and and_3 (and_3_out, not_1_out, X[7]);
  assign not_3_out = ~Y;  // NOT_Gate not_3, 8 bits wide
  Comparator comparator_1 (.a(Y), .b(X), .eq(EQ));  // open: gt, lt
  not not_4 (not_4_out, OpCode[2]);
  and and_4 (and_4_out, not_4_out, OpCode[1]);
  and and_5 (and_5_out, and_1_out, not_5_out);
  nor nor_1 (nor_1_out, Y[7], X[7]);
  and and_6 (and_6_out, nor_1_out, out_5[7]);
  and and_7 (and_7_out, and_2_out, out_5[7]);
  and and_8 (and_8_out, and_3_out, not_5_out);
  not not_5 (not_5_out, out_5[7]);
  not not_6 (not_6_out, OpCode[0]);
  and and_9 (and_9_out, not_6_out, and_4_out);
  and and_10 (and_10_out, and_4_out, OpCode[0]);
  Comparator comparator_2 (.a(X), .b(Y), .eq(comparator_2_eq));  // open: gt, lt
  assign OR_out = Y | X;  // OR_Gate OR, 8 bits wide
  assign AND_11_out = Y & X;  // AND_Gate AND_11, 8 bits wide
  Adder adder_1 (.a(Y), .b(X), .out(adder_1_out), .cin(1'b0), .cout(out_4));
  Adder adder_2 (.a(X), .b(not_3_out), .out(adder_2_out), .cin(1'b1), .cout(out_6));
  Shifter shifter_1 (.in(X), .\dist (Y[2:0]), .out(shifter_1_out));
  Shifter #(.shift("lr")) shifter_2 (.in(X), .\dist (Y[2:0]), .out(shifter_2_out));
  Shifter #(.shift("ar")) shifter_3 (.in(X), .\dist (Y[2:0]), .out(shifter_3_out));
  and and_12 (and_12_out, out_4, and_9_out);
  not not_7 (not_7_out, out_6);
  or or_2 (or_2_out, and_5_out, and_6_out);
  and and_13 (and_13_out, or_2_out, and_9_out);
  and and_14 (and_14_out, and_10_out, or_3_out);
  or or_3 (or_3_out, and_7_out, and_8_out);
  not not_8 (not_8_out, comparator_2_eq);
  and and_15 (and_15_out, not_7_out, and_10_out);
  or or_4 (OF, and_13_out, and_14_out);
  assign bit_extender_1_out = {{7{1'b0}}, not_8_out};  // Bit_Extender bit_extender_1
  or or_5 (CF, and_12_out, and_15_out);
  // Probe on bit_extender_1_out
  // Probe on OR_out
  // Probe on AND_11_out
  // Probe on adder_1_out
  // Probe on adder_2_out
  // Probe on shifter_1_out
  // Probe on shifter_2_out
  // Probe on shifter_3_out
  Multiplexer #(.select(3), .width(8)) multiplexer_1 (
    .in0(OR_out), .in1(AND_11_out), .in2(adder_1_out), .in3(adder_2_out), .in4(shifter_1_out),
    .in5(shifter_2_out), .in6(shifter_3_out), .in7(bit_extender_1_out), .out(out_5), .sel(OpCode));  // open: en
  nor nor_2 (ZF, out_5[7], out_5[6], out_5[5], out_5[4], out_5[3], out_5[2], out_5[1], out_5[0]);

  assign CF_2 = CF;
  assign EQ_2 = EQ;
  assign OF_2 = OF;
  assign SF = out_5[7];
  assign SF_2 = out_5[7];
  assign ZF_2 = ZF;

  // Notes on the sheet:
  //   cs31 lab3, part 2: ALU
endmodule
